// Logisim project homework.circ as structural Verilog: 9 circuits, main circuit DEC_2To4
module main (
  input  in_1,
  input  in_2,
  input  in_3,
  input  in_4,
  input  in_5,
  input  in_6,
  input  in_7,
  input  in_8,
  input  in_9,
  input  in_10,
  input  in_11,
  input  in_12,
  input  in_13,
  input  in_14,
  input  in_15,
  input  in_16
);

  wire and_1_out, dec_2to4_1_y0, dec_2to4_1_y1, dec_2to4_1_y2, dec_2to4_1_y3, dec_3to8_1_y1, dec_3to8_1_y2,
       dec_3to8_1_y3, dec_3to8_1_y4, dec_3to8_1_y5, dec_3to8_1_y6, dec_3to8_1_y7, dec_3to8_1_y8, nand_1_out,
       nand_2_out, nand_3_out, not_1_out, or_1_out, or_2_out, shumaguan_1_a, shumaguan_1_b, shumaguan_1_c,
       shumaguan_1_d, shumaguan_1_e, shumaguan_1_f, shumaguan_1_g;

  nand nand_1 (nand_1_out, in_1, in_2);
  or or_1 (or_1_out, in_1, in_2);
  nand nand_2 (nand_2_out, in_3, in_4);
  or or_2 (or_2_out, in_3, in_4);
  Hex_Digit_Display TEST (.value({in_15, in_14, in_13, in_12}));  // open: dp
  and and_1 (and_1_out, nand_1_out, or_1_out);
  LED XOR_OUT (.in(and_1_out));
  nand nand_3 (nand_3_out, nand_2_out, or_2_out);
  LED XNOR_OUT (.in(nand_3_out));
  not not_1 (not_1_out, in_16);
  LED led_1 (.in(dec_2to4_1_y0));
  DEC_2To4 dec_2to4_1 (
    .A0(in_5), .A1(in_6), .EN(in_7), .Y0(dec_2to4_1_y0), .Y1(dec_2to4_1_y1), .Y2(dec_2to4_1_y2),
    .Y3(dec_2to4_1_y3));
  LED led_2 (.in(dec_2to4_1_y1));
  LED led_3 (.in(dec_2to4_1_y2));
  LED led_4 (.in(dec_2to4_1_y3));
  DEC_3To8 dec_3to8_1 (
    .A0(in_8), .A1(in_9), .A2(in_10), .EN(in_11), .Y1(dec_3to8_1_y1), .Y2(dec_3to8_1_y2), .Y3(dec_3to8_1_y3),
    .Y4(dec_3to8_1_y4), .Y5(dec_3to8_1_y5), .Y6(dec_3to8_1_y6), .Y7(dec_3to8_1_y7), .Y8(dec_3to8_1_y8));
  shumaguan shumaguan_1 (
    .A0(in_12), .A1(in_13), .A2(in_14), .A3(in_15), .EN(in_16), .A(shumaguan_1_a), .B(shumaguan_1_b),
    .C(shumaguan_1_c), .D(shumaguan_1_d), .E(shumaguan_1_e), .F(shumaguan_1_f), .G(shumaguan_1_g));
  LedBar ledbar_1 (
    .led0(dec_3to8_1_y1), .led1(dec_3to8_1_y2), .led2(dec_3to8_1_y3), .led3(dec_3to8_1_y4),
    .led4(dec_3to8_1_y5), .led5(dec_3to8_1_y6), .led6(dec_3to8_1_y7), .led7(dec_3to8_1_y8));
  _7_Segment_Display u_7_segment_display_1 (
    .g(shumaguan_1_g), .f(shumaguan_1_f), .a(shumaguan_1_a), .b(shumaguan_1_b), .e(shumaguan_1_e),
    .d(shumaguan_1_d), .c(shumaguan_1_c), .dp(not_1_out));
endmodule

module DEC_1To2 (
  input  A0,
  output Y0,
  output Y1
);

  not not_1 (Y0, A0);

  assign Y1 = A0;
endmodule

module DEC_2To4 (
  input  A0,
  input  A1,
  input  EN,
  output Y0,
  output Y1,
  output Y2,
  output Y3
);

  wire not_1_out, not_2_out;

  not not_1 (not_1_out, A0);
  not not_2 (not_2_out, A1);
  and and_1 (Y0, not_1_out, EN, not_2_out);
  and and_2 (Y1, not_1_out, EN, A1);
  and and_3 (Y2, A0, EN, not_2_out);
  and and_4 (Y3, A0, EN, A1);
endmodule

module DEC_3To8 (
  input  A0,
  input  A1,
  input  A2,
  input  EN,
  output Y1,
  output Y2,
  output Y3,
  output Y4,
  output Y5,
  output Y6,
  output Y7,
  output Y8
);

  wire and_1_out, and_2_out, not_1_out;

  not not_1 (not_1_out, A2);
  and and_1 (and_1_out, not_1_out, EN);
  and and_2 (and_2_out, A2, EN);
  DEC_2To4 dec_2to4_1 (.A0(A1), .A1(A0), .EN(and_1_out), .Y0(Y1), .Y1(Y2), .Y2(Y3), .Y3(Y4));
  DEC_2To4 dec_2to4_2 (.A0(A1), .A1(A0), .EN(and_2_out), .Y0(Y5), .Y1(Y6), .Y2(Y7), .Y3(Y8));
endmodule

module DEC_4To16 (
  input  A0,
  input  A1,
  input  A2,
  input  A3,
  input  EN,
  output Y0,
  output Y1,
  output Y2,
  output Y3,
  output Y4,
  output Y5,
  output Y6,
  output Y7,
  output Y8,
  output Y9,
  output Y10,
  output Y11,
  output Y12,
  output Y13,
  output Y14,
  output Y15
);

  wire and_1_out, and_2_out, not_1_out;

  not not_1 (not_1_out, A3);
  and and_1 (and_1_out, EN, A3);
  and and_2 (and_2_out, not_1_out, EN);
  DEC_3To8 dec_3to8_1 (
    .A0(A0), .A1(A1), .A2(A2), .EN(and_2_out), .Y1(Y0), .Y2(Y1), .Y3(Y2), .Y4(Y3), .Y5(Y4), .Y6(Y5), .Y7(Y6),
    .Y8(Y7));
  DEC_3To8 dec_3to8_2 (
    .A0(A0), .A1(A1), .A2(A2), .EN(and_1_out), .Y1(Y8), .Y2(Y9), .Y3(Y10), .Y4(Y11), .Y5(Y12), .Y6(Y13),
    .Y7(Y14), .Y8(Y15));
endmodule

module shumaguan (
  input  A0,
  input  A1,
  input  A2,
  input  A3,
  input  EN,
  output A,
  output B,
  output C,
  output D,
  output E,
  output F,
  output G
);

  wire dec_4to16_1_y0, dec_4to16_1_y1, dec_4to16_1_y2, dec_4to16_1_y3, dec_4to16_1_y4, dec_4to16_1_y5,
       dec_4to16_1_y6, dec_4to16_1_y7, dec_4to16_1_y8, dec_4to16_1_y9, dec_4to16_1_y10, dec_4to16_1_y11,
       dec_4to16_1_y12, dec_4to16_1_y13, dec_4to16_1_y14, dec_4to16_1_y15;

  DEC_4To16 dec_4to16_1 (
    .A0(A0), .A1(A1), .A2(A2), .A3(A3), .EN(EN), .Y0(dec_4to16_1_y0), .Y1(dec_4to16_1_y1),
    .Y2(dec_4to16_1_y2), .Y3(dec_4to16_1_y3), .Y4(dec_4to16_1_y4), .Y5(dec_4to16_1_y5), .Y6(dec_4to16_1_y6),
    .Y7(dec_4to16_1_y7), .Y8(dec_4to16_1_y8), .Y9(dec_4to16_1_y9), .Y10(dec_4to16_1_y10),
    .Y11(dec_4to16_1_y11), .Y12(dec_4to16_1_y12), .Y13(dec_4to16_1_y13), .Y14(dec_4to16_1_y14),
    .Y15(dec_4to16_1_y15));
  or or_1 (A, dec_4to16_1_y0, dec_4to16_1_y2, dec_4to16_1_y3, dec_4to16_1_y5, dec_4to16_1_y6, dec_4to16_1_y7, dec_4to16_1_y8, dec_4to16_1_y9, dec_4to16_1_y10, dec_4to16_1_y12, dec_4to16_1_y14, dec_4to16_1_y15);
  or or_2 (B, dec_4to16_1_y0, dec_4to16_1_y1, dec_4to16_1_y2, dec_4to16_1_y3, dec_4to16_1_y4, dec_4to16_1_y7, dec_4to16_1_y8, dec_4to16_1_y9, dec_4to16_1_y10, dec_4to16_1_y13);
  or or_3 (C, dec_4to16_1_y0, dec_4to16_1_y1, dec_4to16_1_y3, dec_4to16_1_y4, dec_4to16_1_y5, dec_4to16_1_y6, dec_4to16_1_y7, dec_4to16_1_y8, dec_4to16_1_y9, dec_4to16_1_y10, dec_4to16_1_y11, dec_4to16_1_y13);
  or or_4 (D, dec_4to16_1_y0, dec_4to16_1_y2, dec_4to16_1_y3, dec_4to16_1_y5, dec_4to16_1_y6, dec_4to16_1_y8, dec_4to16_1_y9, dec_4to16_1_y11, dec_4to16_1_y12, dec_4to16_1_y13, dec_4to16_1_y14);
  or or_5 (E, dec_4to16_1_y0, dec_4to16_1_y2, dec_4to16_1_y6, dec_4to16_1_y8, dec_4to16_1_y10, dec_4to16_1_y11, dec_4to16_1_y12, dec_4to16_1_y13, dec_4to16_1_y14, dec_4to16_1_y15);
  or or_6 (F, dec_4to16_1_y0, dec_4to16_1_y4, dec_4to16_1_y5, dec_4to16_1_y6, dec_4to16_1_y8, dec_4to16_1_y9, dec_4to16_1_y10, dec_4to16_1_y11, dec_4to16_1_y12, dec_4to16_1_y14, dec_4to16_1_y15);
  or or_7 (G, dec_4to16_1_y2, dec_4to16_1_y3, dec_4to16_1_y4, dec_4to16_1_y5, dec_4to16_1_y6, dec_4to16_1_y8, dec_4to16_1_y9, dec_4to16_1_y10, dec_4to16_1_y11, dec_4to16_1_y13, dec_4to16_1_y14, dec_4to16_1_y15);
endmodule

module ENC_16To4 (
  input  in_1,
  input  in_2,
  input  in_3,
  input  in_4,
  input  in_5,
  input  in_6,
  input  in_7,
  input  in_8,
  input  in_9,
  input  in_10,
  input  in_11,
  input  in_12,
  input  in_13,
  input  in_14,
  input  in_15,
  input  in_16
);
endmodule

module Half_Adder (
  input  A0,
  input  A1,
  output SUM,
  output CAL
);

  xor xor_1 (SUM, A0, A1);
  and and_1 (CAL, A0, A1);
endmodule

module Full_Adder (
  input  in_1,
  input  in_2,
  input  in_3,
  output SUM,
  output CAL
);

  wire half_adder_1_cal, half_adder_1_sum, half_adder_2_cal;

  Half_Adder half_adder_1 (.A0(in_1), .A1(in_2), .SUM(half_adder_1_sum), .CAL(half_adder_1_cal));
  Half_Adder half_adder_2 (.A0(half_adder_1_sum), .A1(in_3), .SUM(SUM), .CAL(half_adder_2_cal));
  or or_1 (CAL, half_adder_2_cal, half_adder_1_cal);
endmodule
